# Fritzing sketch bunny (saved by Fritzing 0.9.2b)
breadboards: 1

parts:
  Part1 = RedBear-Duo
  R1 = Resistor [tolerance=±5% resistance=2.2k package=THT]
  LED1 = RGB LED (com. cathode, rgb) [package="5 mm [THT]"]
  U1 = mystery part, 3 pins [chip_label="Hall Effect"]
  R2 = Resistor [tolerance=±5% resistance=10k package=THT]
  R3 = Resistor [tolerance=±5% resistance=2.2k package=THT]
  R5 = Resistor [tolerance=±5% resistance=10k package=THT]
  R4 = Resistor [tolerance=±5% resistance=2.2k package=THT]
  R6 = Photocell (LDR) [package=THT]
  J1 = Basic Force Sensing Resistor (FSR) [package=THT]
  R7 = Resistor [tolerance=±5% resistance=10k package=THT]

nets:
  N1: Part1.A0, J1.pin_0, R7.Pin_0
  N2: Part1.A1, U1.pin1, R2.Pin_0
  N3: Part1.A3, R5.Pin_1, R6.pin_1
  N4: Part1.GND, R5.Pin_0, R7.Pin_1
  N5: Part1.D0, R4.Pin_0
  N6: Part1.D1, R3.Pin_0
  N7: Part1.D2, R1.Pin_0
  N8: Part1.3V3, LED1.common_cathode, U1.pin2, U1.pin3, R2.Pin_1, R6.pin_0, J1.pin_1
  N9: R1.Pin_1, LED1.blue_anode
  N10: LED1.red_anode, R4.Pin_1
  N11: LED1.green_anode, R3.Pin_1

custom parts:
  RedBear-Duo: Duo is a thumb-size development board made to simplify the building process of Internet of Things (IoT). This part is a modification of the Particle Photon part by Brett Walach,Fabian Althaus
