# Fritzing sketch checkin (saved by Fritzing 0.9.2b)
breadboards: 1

parts:
  Part1 = RedBear-Duo
  R4 = Resistor [tolerance=±5% resistance=2.2k package=THT]
  R5 = Resistor [tolerance=±5% resistance=2.2k package=THT]
  R6 = Resistor [tolerance=±5% resistance=2.2k package=THT]
  R7 = Photocell (LDR) [package=THT]
  LED1 = RGB LED - (4 legs) [package="5 mm [THT]"]
  POT1 = Breadboard Trimpot
  POT2 = Breadboard Trimpot
  POT3 = Breadboard Trimpot
  R8 = Resistor [tolerance=±5% resistance=2.2k package=THT]

nets:
  N1: Part1.A0, POT3.PIN2
  N2: Part1.A1, Part1.A3, Part1.A5, Part1.WKP, Part1.TX, Part1.VIN, R7.pin_0, POT2.PIN2, R8.Pin_0
  N3: Part1.A2, POT1.PIN2
  N4: Part1.A4, Part1.RX
  N5: Part1.GND, Part1.D0, Part1.D2, R4.Pin_1, R6.Pin_1, POT1.PIN3, POT2.PIN3, POT3.PIN3, R8.Pin_1
  N6: Part1.D1, R5.Pin_1
  N7: Part1.D3, Part1.D5, Part1.D7, Part1.VBAT, Part1.3V3, R7.pin_1, LED1.common_anode, POT1.PIN1, POT2.PIN1, POT3.PIN1
  N8: Part1.D4, Part1.D6
  N9: R4.Pin_0, LED1.blue_cathode
  N10: R5.Pin_0, LED1.green_cathode
  N11: R6.Pin_0, LED1.red_cathode

notes:
  Common Anode, connect long pin of LED to +3.3V
  LEDs on D[0:2] for PWM
  Trimpots connected to A[0:2]
  Photocell has 2.2k ohm pulldown

custom parts:
  RedBear-Duo: Duo is a thumb-size development board made to simplify the building process of Internet of Things (IoT). This part is a modification of the Particle Photon part by Brett Walach,Fabian Althaus
