# Fritzing sketch facetracker (saved by Fritzing 0.9.2b)
breadboards: 1

parts:
  Part1 = RedBear-Duo
  J1 = Piezo Speaker
  Part2 = SRF05 Ultrasonic Rangefinder
  J2 = Basic Servo
  VCC1 = 4 x AAA Battery Mount
  LED2 = RGB LED - (4 legs) [package="5 mm [THT]"]
  R2 = Resistor [tolerance=±5% resistance=2.2k package=THT]
  R3 = Resistor [tolerance=±5% resistance=2.2k package=THT]
  R4 = Resistor [tolerance=±5% resistance=2.2k package=THT]

nets:
  N1: Part1.A0, Part2.Trig
  N2: Part1.A1, Part2.Echo
  N3: Part1.WKP, J1.pin2
  GND: Part1.GND, J1.pin1, Part2.GND, J2.gnd, VCC1.-
  N4: Part1.D0, R3.Pin_0
  N5: Part1.D1, R4.Pin_0
  N6: Part1.D2, R2.Pin_0
  N7: Part1.D3, J2.pulse
  3V3: Part1.3V3, Part2.VCC, LED2.common_anode
  N8: J2.vcc, VCC1.+
  N9: LED2.red_cathode, R4.Pin_1
  N10: LED2.green_cathode, R3.Pin_1
  N11: LED2.blue_cathode, R2.Pin_1

notes:
  Pretend this is 3 batteries

custom parts:
  RedBear-Duo: Duo is a thumb-size development board made to simplify the building process of Internet of Things (IoT). This part is a modification of the Particle Photon part by Brett Walach,Fabian Althaus
